# Fritzing sketch Rotary Encoder Mini Board (saved by Fritzing 0.8.5b)
circuit board: 2.47651cm x 2.17906cm
breadboards: 1

parts:
  ENCODER2 = Rotary Encoder with Knob
  220 = Resistor [tolerance=±5% resistance=10k package=THT]
  10K = Resistor [tolerance=±5% resistance=10k package=THT]
  10K_2 = Resistor [tolerance=±5% resistance=220 package=THT]
  J8 = female pin header, 5 pins [form="♀ (female)"]

nets:
  N1: ENCODER2.no_name_yet#1, 220.Pin_1, J8.pin5
  N2: ENCODER2.no_name_yet#2, 10K_2.Pin_1, J8.pin4
  GND: ENCODER2.no_name_yet#3, 10K.Pin_1, J8.pin3
  N3: ENCODER2.no_name_yet#4, 220.Pin_0, 10K.Pin_0, J8.pin2
  N4: ENCODER2.no_name_yet#5, 10K_2.Pin_0, J8.pin1

custom parts:
  Rotary Encoder with Knob: Rotary Encoder with 1/4" Shaft and Knob
